# Fritzing sketch motor (saved by Fritzing 0.9.3b)

parts:
  S1 = H-Bridge with L298N
  M1 = DC Motor
  M2 = DC Motor
  元件1 = Arduino Mega 2560 (Rev3)
  VCC1 = Battery block 9V

nets:
  N1: S1.12V, VCC1.+
  N2: S1.GND, VCC1.-
  N3: S1.IN1, 元件1.D6_PWM
  N4: S1.IN2, 元件1.D5_PWM
  N5: S1.IN3, 元件1.D4_PWM
  N6: S1.IN4, 元件1.D3_PWM
  N7: S1.M1-01, M1.pin_2
  N8: S1.M1-02, M1.pin_1
  N9: S1.M2-01, M2.pin_2
  N10: S1.M2-02, M2.pin_1

notes:
  A
  B
  C
  D
  E

custom parts:
  H-Bridge with L298N: h-bridge
